# Fritzing sketch PiRIS (saved by Fritzing 0.9.3b)
breadboards: 1

parts:
  S1 = Pushbutton [package="[THT]"]
  S2 = Pushbutton [package="[THT]"]
  S3 = Pushbutton [package="[THT]"]
  S4 = Pushbutton [package="[THT]"]
  Raspberry_Pi_1 = Raspberry Pi 3 [part_number=RPI-3-V1.2]  # not connected

nets:
  N1: S1.Pin_1, S1.Pin_2, S2.Pin_1, S2.Pin_2, S3.Pin_1, S3.Pin_2, S4.Pin_1, S4.Pin_2
  N2: S1.Pin_3, S1.Pin_4
  N3: S2.Pin_3, S2.Pin_4
  N4: S3.Pin_3, S3.Pin_4
  N5: S4.Pin_3, S4.Pin_4

notes:
  [54 to 51 are GPIO 22-25]
  The Breakout Board is locally designed and made. Unreplicable
  Buttons are 3x3 and 2 pins, not 3x4 and 4 pins.
